# Fritzing sketch i2c_communication_between_uno_mega (saved by Fritzing 0.9.3b)

parts:
  Part1 = Arduino Uno (Rev3)
  Part2 = Arduino Mega ADK (Rev3)

nets:
  N1: Part1.A4/SDA, Part2.D20/SDA
  N2: Part1.A5/SCL, Part2.D21/SCL
  GND: Part1.GND, Part2.GND
